# Fritzing sketch fritzing (saved by Fritzing 0.9.6b)
breadboards: 1

parts:
  U1 = attiny85 [package=dip]
  IC2 = Voltage Regulator [part_number=7805 package=to220-igo]
  J1 = Screw terminal - 2 pins [package=THT]
  C3 = Electrolytic Capacitor [capacitance=100µF voltage=35V package="0605 [SMD, electrolytic]"]
  C4 = Electrolytic Capacitor [capacitance=100µF voltage=35V package="0605 [SMD, electrolytic]"]
  C5 = Ceramic Capacitor [capacitance=100nF voltage=35V package="100 mil [THT, multilayer]"]
  C6 = Ceramic Capacitor [capacitance=100nF voltage=35V package="100 mil [THT, multilayer]"]
  R1 = Resistor [tolerance=±5% resistance=10k package="0402 [SMD]"]
  R2 = Resistor [tolerance=±5% resistance=10k package="0402 [SMD]"]
  C7 = Ceramic Capacitor [capacitance=100nF voltage=35V package="100 mil [THT, multilayer]"]
  R3 = Temperature Sensor (Thermistor) [thermistor_type=NTC package=THT]
  F1 = Fan - 4 wire [package=THT]
  R4 = Resistor [tolerance=±5% resistance=1k package="0402 [SMD]"]

nets:
  N1: U1.Pin_1, R1.Pin_1, C7.1
  N2: U1.Pin_2, R2.Pin_1, R3.pin_1
  GND: U1.Pin_4, IC2.GND, J1.pin2, C3.-, C4.-, C5.0, C6.0, C7.0, R3.pin_0, F1.GND
  N3: U1.Pin_5, R4.Pin_0
  5V: U1.Pin_8, IC2.OUT, C4.+, C5.1, R1.Pin_0, R2.Pin_0
  12V: IC2.IN, J1.pin1, C3.+, C6.1, F1.Power
  N4: F1.PWM, F1.Tach, R4.Pin_1

custom parts:
  Fan - 4 wire: Fan, 4 wire with tach.
